// Logisim project 002_SimpleParallelReg.circ as structural Verilog: 1 circuit, main circuit main
module main (
  input  in_1,
  input  in_2,
  input  in_3,
  input  in_4
);

  wire clock_1_out;

  Clock clock_1 (.out(clock_1_out));
  D_Flip_Flop d_ff_1 (.clk(clock_1_out), .D(in_1), .en(1'b1));  // open: Q, Qn, preset, reset
  D_Flip_Flop d_ff_2 (.clk(clock_1_out), .D(in_2), .en(1'b1));  // open: Q, Qn, preset, reset
  D_Flip_Flop d_ff_3 (.clk(clock_1_out), .D(in_3), .en(1'b1));  // open: Q, Qn, preset, reset
  D_Flip_Flop d_ff_4 (.clk(clock_1_out), .D(in_4), .en(1'b1));  // open: Q, Qn, preset, reset
endmodule
