// Logisim project 004_MpuComponents.circ as structural Verilog
module _8_bit_gate (
  input  [7:0] Input,
  input  Enable,
  output [7:0] Output
);

  assign Output = Enable ? Input : 8'bz;  // Controlled_Buffer controlled_buffer_1
endmodule

module _74173 (
  input  Clock,
  input  D0,
  input  D1,
  input  D2,
  input  D3,
  input  IE0,
  input  IE1,
  input  MR,
  input  OE0,
  input  OE1,
  output O0,
  output O1,
  output O2,
  output O3
);

  wire and_1_out, and_2_out, controlled_buffer_1_out, controlled_buffer_2_out, controlled_buffer_3_out,
       controlled_buffer_4_out, d_ff_1_q, d_ff_2_q, d_ff_3_q, d_ff_4_q, not_1_out, not_2_out, not_3_out,
       not_4_out;

  assign controlled_buffer_1_out = and_1_out ? D0 : 1'bz;  // Controlled_Buffer controlled_buffer_1
  assign controlled_buffer_2_out = and_1_out ? D1 : 1'bz;  // Controlled_Buffer controlled_buffer_2
  assign controlled_buffer_3_out = and_1_out ? D2 : 1'bz;  // Controlled_Buffer controlled_buffer_3
  assign controlled_buffer_4_out = and_1_out ? D3 : 1'bz;  // Controlled_Buffer controlled_buffer_4
  not not_1 (not_1_out, IE0);
  and and_1 (and_1_out, not_1_out, not_2_out);
  not not_2 (not_2_out, IE1);
  not not_3 (not_3_out, OE0);
  and and_2 (and_2_out, not_3_out, not_4_out);
  not not_4 (not_4_out, OE1);
  D_Flip_Flop d_ff_1 (
    .clk(Clock), .D(controlled_buffer_1_out), .Q(d_ff_1_q), .en(1'b1), .reset(MR));  // open: Qn, preset
  D_Flip_Flop d_ff_2 (
    .clk(Clock), .D(controlled_buffer_2_out), .Q(d_ff_2_q), .en(1'b1), .reset(MR));  // open: Qn, preset
  D_Flip_Flop d_ff_3 (
    .clk(Clock), .D(controlled_buffer_3_out), .Q(d_ff_3_q), .en(1'b1), .reset(MR));  // open: Qn, preset
  D_Flip_Flop d_ff_4 (
    .clk(Clock), .D(controlled_buffer_4_out), .Q(d_ff_4_q), .en(1'b1), .reset(MR));  // open: Qn, preset
  assign O0 = and_2_out ? d_ff_1_q : 1'bz;  // Controlled_Buffer controlled_buffer_5
  assign O1 = and_2_out ? d_ff_2_q : 1'bz;  // Controlled_Buffer controlled_buffer_6
  assign O2 = and_2_out ? d_ff_3_q : 1'bz;  // Controlled_Buffer controlled_buffer_7
  assign O3 = and_2_out ? d_ff_4_q : 1'bz;  // Controlled_Buffer controlled_buffer_8
endmodule

module main (
);

  _74173 u_74173_1 ();  // open: D0, D1, D2, D3, IE0, IE1, MR, OE0, OE1, O0, O1, O2, O3, Clock
endmodule

module Register_Common_IO (
  input  en,
  input  R_w,
  input  D3,
  input  D2,
  input  D1,
  input  D0,
  output D3_2,
  output D2_2,
  output D1_2,
  output D0_2
);

  wire clock_1_out, controlled_buffer_1_out, controlled_buffer_2_out, controlled_buffer_3_out,
       controlled_buffer_4_out, d_ff_1_q, d_ff_2_q, d_ff_3_q, d_ff_4_q, en_t, R_W_prime;

  not not_1 (en_t, en);
  not not_2 (R_W_prime, R_w);
  Clock clock_1 (.out(clock_1_out));
  assign controlled_buffer_1_out = R_W_prime ? D3 : 1'bz;  // Controlled_Buffer controlled_buffer_1
  assign controlled_buffer_2_out = R_W_prime ? D2 : 1'bz;  // Controlled_Buffer controlled_buffer_2
  assign controlled_buffer_3_out = R_W_prime ? D1 : 1'bz;  // Controlled_Buffer controlled_buffer_3
  assign controlled_buffer_4_out = R_W_prime ? D0 : 1'bz;  // Controlled_Buffer controlled_buffer_4
  D_Flip_Flop d_ff_1 (
    .clk(clock_1_out), .D(controlled_buffer_1_out), .Q(d_ff_1_q), .en(en_t));  // open: Qn, preset, reset
  D_Flip_Flop d_ff_2 (
    .clk(clock_1_out), .D(controlled_buffer_2_out), .Q(d_ff_2_q), .en(en_t));  // open: Qn, preset, reset
  D_Flip_Flop d_ff_3 (
    .clk(clock_1_out), .D(controlled_buffer_3_out), .Q(d_ff_3_q), .en(en_t));  // open: Qn, preset, reset
  D_Flip_Flop d_ff_4 (
    .clk(clock_1_out), .D(controlled_buffer_4_out), .Q(d_ff_4_q), .en(en_t));  // open: Qn, preset, reset
  assign D3_2 = R_w ? d_ff_1_q : 1'bz;  // Controlled_Buffer controlled_buffer_5
  assign D2_2 = R_w ? d_ff_2_q : 1'bz;  // Controlled_Buffer controlled_buffer_6
  assign D1_2 = R_w ? d_ff_3_q : 1'bz;  // Controlled_Buffer controlled_buffer_7
  assign D0_2 = R_w ? d_ff_4_q : 1'bz;  // Controlled_Buffer controlled_buffer_8
endmodule

module Memory_Demo (
  input  [7:0] in_1,
  input  [1:0] CS,
  output [7:0] out_3
);

  wire clock_1_out, n2_4_encoder_1_o0, n2_4_encoder_1_o1, n2_4_encoder_1_o2, n2_4_encoder_1_o3;

  _2_4_Encoder u_2_4_encoder_1 (
    .I0(CS[1]), .I1(CS[0]), .O0(n2_4_encoder_1_o0), .O1(n2_4_encoder_1_o1), .O2(n2_4_encoder_1_o2),
    .O3(n2_4_encoder_1_o3));
  Clock clock_1 (.out(clock_1_out));
  RAM ram_1 (.addr(in_1), .data(out_3), .sel(n2_4_encoder_1_o0), .clk(clock_1_out));  // open: ld, clr
  RAM ram_2 (.addr(in_1), .data(out_3), .sel(n2_4_encoder_1_o1), .clk(clock_1_out));  // open: ld, clr
  RAM ram_3 (.addr(in_1), .data(out_3), .sel(n2_4_encoder_1_o2), .clk(clock_1_out));  // open: ld, clr
  RAM ram_4 (.sel(n2_4_encoder_1_o3), .clk(clock_1_out));  // open: addr, data, ld, clr
  ROM rom_1 ();  // open: addr, data, sel
endmodule

module _2_4_Encoder (
  input  I0,
  input  I1,
  output O0,
  output O1,
  output O2,
  output O3
);

  wire not_1_out, not_2_out, not_3_out, not_4_out;

  not not_1 (not_1_out, I0);
  not not_2 (not_2_out, I1);
  not not_3 (not_3_out, I0);
  not not_4 (not_4_out, I1);
  and and_1 (O3, I0, I1);
  and and_2 (O0, not_1_out, not_2_out);
  and and_3 (O1, not_3_out, I1);
  and and_4 (O2, I0, not_4_out);
endmodule
