// Logisim project 005_Basic_MPU.circ as structural Verilog: 6 circuits, main circuit main
// flags
module main (
  input  in_1
);

  wire Clk, Jump_Enabled, JZE, RST, Stack_Enabled, TTY_Enabled, Write_Enabled;
  wire [1:0] Register_Data_Select;
  wire [2:0] Addr_A, Addr_B, alu_1_alu_flags, ALU_Function, Write_Addr;
  wire [3:0] ALU_Data, DataA, DataB, multiplexer_1_out, op_code, Stack_Data;
  wire [3:3] Write_Data;
  wire [7:0] Count, Jump_Address;
  wire [11:7] rom_1_data;

  Clock SysClk (.out(Clk));
  Button Reset (.out(RST));
  // Probe on op_code
  ROM #(.dataWidth(16)) rom_1 (
    .addr(Count), .data({op_code, rom_1_data[11], Write_Addr, rom_1_data[7], Addr_A, Write_Data[3], Addr_B}));  // open: sel
  _8_bit_Counter Program_Counter (
    .Jump_Address(Jump_Address), .Count(Count), .Clock(Clk), .Dec(in_1), .Clear(RST),
    .Jump_Enabled(Jump_Enabled));
  // Probe on {op_code, rom_1_data[11], Write_Addr, rom_1_data[7], Addr_A, Write_Data[3], Addr_B}
  ROM #(.addrWidth(4)) rom_2 (
    .addr(op_code), .data({ALU_Function, Register_Data_Select, TTY_Enabled, Stack_Enabled, Write_Enabled}));  // open: sel
  // Probe on op_code
  // Probe on ALU_Function
  // Probe on Write_Addr
  ALU alu_1 (
    .Data_A(DataA), .Data_B(DataB), .ALU_Function(ALU_Function), .ALU_Out(ALU_Data),
    .ALU_Flags(alu_1_alu_flags), .Jump_Zero_Enabled(JZE), .Jump_Enabled(Jump_Enabled));
  // Probe on alu_1_alu_flags
  Multiplexer #(.select(2), .width(4), .enable("false")) multiplexer_1 (
    .in0({Write_Data[3], Addr_B}), .in1(ALU_Data), .in2(DataA), .in3(Stack_Data), .out(multiplexer_1_out),
    .sel(Register_Data_Select));
  // Probe on Addr_A
  // Probe on Register_Data_Select
  // Probe on Addr_B
  // Probe on TTY_Enabled
  TTY tty_1 (.data({DataA[2:0], DataB}), .clk(Clk), .we(TTY_Enabled), .clr(RST));
  // Probe on Count
  RegisterFile Register_File (
    .Clock(Clk), .Data_In(multiplexer_1_out), .Write_Enable(Write_Enabled), .Write_Address(Write_Addr),
    .Read_Address_A(Addr_A), .Data_A(DataA), .Data_B(DataB), .Read_Address_B(Addr_B));
  // Probe on {Write_Data[3], Addr_B}
  // Probe on Stack_Enabled
  // Probe on Jump_Address
  // Probe on DataA
  // Probe on Write_Enabled
  // Probe on DataB
  Stack File_Stack (
    .Enabled(Stack_Enabled), .Push_Pop(Write_Enabled), .Push_Data({Write_Data[3], Addr_B}),
    .Pop_Data(Stack_Data), .Clock(Clk));
  Multiplexer #(.width(8), .enable("false")) multiplexer_2 (
    .in0({DataB, DataA}), .in1({1'b0, Write_Addr, Write_Data[3], Addr_B}), .out(Jump_Address), .sel(JZE));

  // Other names for the same wires on the sheet: Write_Data[2:0] = Addr_B

  // Notes on the sheet:
  //   Program Memory
  //   contents of rom_1 (hex, n*v repeats v):
  //   1000 a109 c100 c000 6201 a029 3001 1700 a072 c000 c100 9001 1600 c100 c000 6206 a124 7101 1700 a07e
  //   1703 3071 c000 c100 9001 b003 b003 b000 b000 b000 b00d b006 b00c b006 b00c b006 b001 b002 b000 b006
  //   b00f b006 b00c b006 b00c b006 b005 b004 b008 1000 a002 b004 b009 b000 b000 b002 b000 b003 b00d b002
  //   b000 b003 b004 b002 b000 b002 b00b b002 b000 b003 b003 1000 a002 b005 b000 b000 b003 b004 1000 a00c
  //   1000 110d 3001 b006 b009 b000 b000 b002 b000 b003 b00d b002 b000 b003 b003 b002 b000 b002 b00a b002
  //   b000 b003 b003 1000 a002 b007 b001 b000 b003 b003 b003 1000 a00c 1000 110d 3001 b008 b00a b000 b000
  //   b002 b000 b003 b00d b002 b000 b003 b003 b002 b000 b002 b00d b002 b000 b003 b004 1000 a002 1004 1103
  //   8110 1201 7112 7210 1703 3072 1000 110d 3001 b00a b00b b000 b000 b002 b000 b003 b00d b002 b000 b003
  //   b002 b002 b000 b002 b00d b002 b000 b003 b005 1000 a002 1005 1102 d201 1703 3072 1000 110d 3001
  //   Instruction Decoder
  //   contents of rom_2 (hex, n*v repeats v):
  //   0 1 11 4 9 29 49 69 89 a8 c0 2 1b e9
endmodule

// GPR
module GPRegister (
  input  Clock,
  input  [3:0] Data_In,
  input  Write,
  output [3:0] Data_Out
);

  wire multiplexer_1_out, multiplexer_2_out, multiplexer_3_out, multiplexer_4_out;

  Multiplexer #(.enable("false")) multiplexer_1 (
    .in0(Data_Out[0]), .in1(Data_In[0]), .out(multiplexer_1_out), .sel(Write));
  Multiplexer #(.enable("false")) multiplexer_2 (
    .in0(Data_Out[1]), .in1(Data_In[1]), .out(multiplexer_2_out), .sel(Write));
  Multiplexer #(.enable("false")) multiplexer_3 (
    .in0(Data_Out[2]), .in1(Data_In[2]), .out(multiplexer_3_out), .sel(Write));
  Multiplexer #(.enable("false")) multiplexer_4 (
    .in0(Data_Out[3]), .in1(Data_In[3]), .out(multiplexer_4_out), .sel(Write));
  D_Flip_Flop d_ff_1 (.clk(Clock), .D(multiplexer_1_out), .Q(Data_Out[0]));  // open: Qn, preset, en, reset
  D_Flip_Flop d_ff_2 (.clk(Clock), .D(multiplexer_2_out), .Q(Data_Out[1]));  // open: Qn, preset, en, reset
  D_Flip_Flop d_ff_3 (.clk(Clock), .D(multiplexer_3_out), .Q(Data_Out[2]));  // open: Qn, preset, en, reset
  D_Flip_Flop d_ff_4 (.clk(Clock), .D(multiplexer_4_out), .Q(Data_Out[3]));  // open: Qn, preset, en, reset
endmodule

module RegisterFile (
  input  Clock,
  input  [3:0] Data_In,
  input  Write_Enable,
  input  [2:0] Write_Address,
  input  [2:0] Read_Address_A,
  input  [2:0] Read_Address_B,
  output [3:0] Data_A,
  output [3:0] Data_B
);

  wire W000, W001, W010, W011, W100, W101, W110, W111;
  wire [3:0] R000, R001, R010, R011, R100, R101, R110, R111;

  GPRegister gpregister_1 (.Data_In(Data_In), .Data_Out(R000), .Clock(Clock), .Write(W000));
  GPRegister gpregister_2 (.Data_In(Data_In), .Data_Out(R001), .Clock(Clock), .Write(W001));
  GPRegister gpregister_3 (.Data_In(Data_In), .Data_Out(R010), .Clock(Clock), .Write(W010));
  GPRegister gpregister_4 (.Data_In(Data_In), .Data_Out(R011), .Clock(Clock), .Write(W011));
  Multiplexer #(.select(3), .width(4), .enable("false")) multiplexer_1 (
    .in0(R000), .in1(R001), .in2(R010), .in3(R011), .in4(R100), .in5(R101), .in6(R110), .in7(R111),
    .out(Data_A), .sel(Read_Address_A));
  GPRegister gpregister_5 (.Data_In(Data_In), .Data_Out(R100), .Clock(Clock), .Write(W100));
  GPRegister gpregister_6 (.Data_In(Data_In), .Data_Out(R101), .Clock(Clock), .Write(W101));
  GPRegister gpregister_7 (.Data_In(Data_In), .Data_Out(R110), .Clock(Clock), .Write(W110));
  GPRegister gpregister_8 (.Data_In(Data_In), .Data_Out(R111), .Clock(Clock), .Write(W111));
  Multiplexer #(.select(3), .width(4), .enable("false")) multiplexer_2 (
    .in0(R000), .in1(R001), .in2(R010), .in3(R011), .in4(R100), .in5(R101), .in6(R110), .in7(R111),
    .out(Data_B), .sel(Read_Address_B));
  Decoder #(.select(3)) decoder_1 (
    .out0(W000), .out1(W001), .out2(W010), .out3(W011), .out4(W100), .out5(W101), .out6(W110), .out7(W111),
    .sel(Write_Address), .en(Write_Enable));
  // Probe on R000
  // Probe on R001
  // Probe on R010
  // Probe on R011
  // Probe on R100
  // Probe on R101
  // Probe on R110
  // Probe on R111
endmodule

module ALU (
  input  [3:0] Data_A,
  input  [3:0] Data_B,
  input  [2:0] ALU_Function,
  output [3:0] ALU_Out,
  output [2:0] ALU_Flags,
  output Jump_Enabled,
  output Jump_Zero_Enabled
);

  wire Add_Zero, adder_1_cout, adder_2_cout, adder_3_cout, adder_5_cout, adder_6_cout, adder_7_cout, Br, Co,
       Jump_Zero, not_5_out, not_6_out, not_7_out, not_8_out, Sub_Zero;
  wire [3:0] ADD, AND, NOT, OR, SUB, XOR;

  nor nor_1 (Jump_Zero, Data_A[0], Data_A[1], Data_A[2], Data_A[3]);
  nor nor_2 (Add_Zero, ADD[0], ADD[1], ADD[2], ADD[3]);
  nor nor_3 (Sub_Zero, SUB[0], SUB[1], SUB[2], SUB[3]);
  xor xor_1 (XOR[0], Data_A[0], Data_B[0]);
  xor xor_2 (XOR[1], Data_A[1], Data_B[1]);
  xor xor_3 (XOR[2], Data_A[2], Data_B[2]);
  xor xor_4 (XOR[3], Data_A[3], Data_B[3]);
  Multiplexer #(.select(3), .width(4), .enable("false")) multiplexer_1 (
    .in0(XOR), .in1(AND), .in2(OR), .in3(ADD), .in4(NOT), .in7(SUB), .out(ALU_Out), .sel(ALU_Function));  // open: in5, in6
  and and_1 (AND[0], Data_A[0], Data_B[0]);
  and and_2 (AND[1], Data_A[1], Data_B[1]);
  and and_3 (AND[2], Data_A[2], Data_B[2]);
  and and_4 (AND[3], Data_A[3], Data_B[3]);
  Multiplexer #(.select(3), .enable("false")) multiplexer_2 (
    .in0(1'b0), .in1(1'b0), .in2(1'b0), .in3(Add_Zero), .in4(1'b0), .in5(1'b0), .in6(1'b0), .in7(Sub_Zero),
    .out(ALU_Flags[0]), .sel(ALU_Function));
  or or_1 (OR[0], Data_A[0], Data_B[0]);
  or or_2 (OR[1], Data_A[1], Data_B[1]);
  or or_3 (OR[2], Data_A[2], Data_B[2]);
  or or_4 (OR[3], Data_A[3], Data_B[3]);
  Multiplexer #(.select(3), .enable("false")) multiplexer_3 (
    .in0(1'b0), .in1(1'b0), .in2(1'b0), .in3(Co), .in4(1'b0), .in5(1'b0), .in6(1'b0), .in7(1'b0),
    .out(ALU_Flags[1]), .sel(ALU_Function));
  Multiplexer #(.select(3), .enable("false")) multiplexer_4 (
    .in0(1'b0), .in1(1'b0), .in2(1'b0), .in3(1'b0), .in4(1'b0), .in5(1'b0), .in6(1'b0), .in7(Br),
    .out(ALU_Flags[2]), .sel(ALU_Function));
  Adder #(.width(1)) adder_1 (.a(Data_A[0]), .b(Data_B[0]), .out(ADD[0]), .cin(1'b0), .cout(adder_1_cout));
  Adder #(.width(1)) adder_2 (.a(Data_A[1]), .b(Data_B[1]), .out(ADD[1]), .cin(adder_1_cout), .cout(adder_2_cout));
  Adder #(.width(1)) adder_3 (.a(Data_A[2]), .b(Data_B[2]), .out(ADD[2]), .cin(adder_2_cout), .cout(adder_3_cout));
  Adder #(.width(1)) adder_4 (.a(Data_A[3]), .b(Data_B[3]), .out(ADD[3]), .cin(adder_3_cout), .cout(Co));
  Multiplexer #(.select(3), .enable("false")) multiplexer_5 (
    .in0(1'b0), .in1(1'b0), .in2(1'b0), .in3(1'b0), .in4(1'b0), .in5(1'b1), .in6(Jump_Zero), .in7(1'b0),
    .out(Jump_Enabled), .sel(ALU_Function));
  not not_1 (NOT[0], Data_A[0]);
  not not_2 (NOT[1], Data_A[1]);
  not not_3 (NOT[2], Data_A[2]);
  not not_4 (NOT[3], Data_A[3]);
  Multiplexer #(.select(3), .enable("false")) multiplexer_6 (
    .in0(1'b0), .in1(1'b0), .in2(1'b0), .in3(1'b0), .in4(1'b0), .in5(1'b0), .in6(Jump_Zero), .in7(1'b0),
    .out(Jump_Zero_Enabled), .sel(ALU_Function));
  not not_5 (not_5_out, Data_B[0]);
  not not_6 (not_6_out, Data_B[1]);
  not not_7 (not_7_out, Data_B[2]);
  not not_8 (not_8_out, Data_B[3]);
  Adder #(.width(1)) adder_5 (.a(Data_A[0]), .b(not_5_out), .out(SUB[0]), .cin(1'b1), .cout(adder_5_cout));
  Adder #(.width(1)) adder_6 (.a(Data_A[1]), .b(not_6_out), .out(SUB[1]), .cin(adder_5_cout), .cout(adder_6_cout));
  Adder #(.width(1)) adder_7 (.a(Data_A[2]), .b(not_7_out), .out(SUB[2]), .cin(adder_6_cout), .cout(adder_7_cout));
  Adder #(.width(1)) adder_8 (.a(Data_A[3]), .b(not_8_out), .out(SUB[3]), .cin(adder_7_cout), .cout(Br));

  // Other names for the same wires on the sheet: Zero = ALU_Flags[0]; Overflow = ALU_Flags[1]; Borrow = ALU_Flags[2]

  // Notes on the sheet:
  //   000-XOR
  //   001-AND
  //   010-OR
  //   101-JMP
  //   011-ADD
  //   100-NOT
  //   110-JZ
  //   111-SUB
endmodule

module _8_bit_Counter (
  input  Clock,
  input  [7:0] Jump_Address,
  input  Dec,
  input  Clear,
  input  Jump_Enabled,
  output [7:0] Count
);

  wire [1:0] or_1_out;
  wire [7:0] C_1, C_1_t, multiplexer_1_out;

  or or_1 (or_1_out[0], Dec, Clear);
  Multiplexer #(.select(2), .width(8), .enable("false")) multiplexer_1 (
    .in0(C_1), .in1(C_1_t), .in2(Jump_Address), .in3({8{1'b0}}), .out(multiplexer_1_out), .sel(or_1_out));
  or or_2 (or_1_out[1], Clear, Jump_Enabled);
  D_Flip_Flop d_ff_1 (.clk(Clock), .D(multiplexer_1_out[0]), .Q(Count[0]));  // open: Qn, preset, en, reset
  D_Flip_Flop d_ff_2 (.clk(Clock), .D(multiplexer_1_out[1]), .Q(Count[1]));  // open: Qn, preset, en, reset
  D_Flip_Flop d_ff_3 (.clk(Clock), .D(multiplexer_1_out[2]), .Q(Count[2]));  // open: Qn, preset, en, reset
  D_Flip_Flop d_ff_4 (.clk(Clock), .D(multiplexer_1_out[3]), .Q(Count[3]));  // open: Qn, preset, en, reset
  D_Flip_Flop d_ff_5 (.clk(Clock), .D(multiplexer_1_out[4]), .Q(Count[4]));  // open: Qn, preset, en, reset
  D_Flip_Flop d_ff_6 (.clk(Clock), .D(multiplexer_1_out[5]), .Q(Count[5]));  // open: Qn, preset, en, reset
  D_Flip_Flop d_ff_7 (.clk(Clock), .D(multiplexer_1_out[6]), .Q(Count[6]));  // open: Qn, preset, en, reset
  D_Flip_Flop d_ff_8 (.clk(Clock), .D(multiplexer_1_out[7]), .Q(Count[7]));  // open: Qn, preset, en, reset
  Adder adder_1 (.a(Count), .b(8'h1), .out(C_1));  // open: cin, cout
  Subtractor subtractor_1 (.a(Count), .b(8'h1), .out(C_1_t));  // open: bin, bout

  // Other names for the same wires on the sheet: C[7:0] = Count; Jump_Addr[7:0] = Jump_Address
endmodule

module Stack (
  input  Clock,
  input  Enabled,
  input  Push_Pop,
  input  [3:0] Push_Data,
  output [3:0] Pop_Data
);

  wire [3:0] gpregister_2_data_out, gpregister_3_data_out, gpregister_4_data_out, gpregister_5_data_out,
       gpregister_6_data_out, gpregister_7_data_out, gpregister_8_data_out, gpregister_9_data_out,
       gpregister_10_data_out, gpregister_11_data_out, gpregister_12_data_out, gpregister_13_data_out,
       gpregister_14_data_out, gpregister_15_data_out, gpregister_16_data_out, gpregister_17_data_out,
       gpregister_18_data_out, gpregister_19_data_out, gpregister_20_data_out, gpregister_21_data_out,
       gpregister_22_data_out, gpregister_23_data_out, gpregister_24_data_out, gpregister_25_data_out,
       gpregister_26_data_out, gpregister_27_data_out, gpregister_28_data_out, gpregister_29_data_out,
       gpregister_30_data_out, gpregister_31_data_out, gpregister_32_data_out, multiplexer_1_out,
       multiplexer_2_out, multiplexer_3_out, multiplexer_4_out, multiplexer_5_out, multiplexer_6_out,
       multiplexer_7_out, multiplexer_8_out, multiplexer_9_out, multiplexer_10_out, multiplexer_11_out,
       multiplexer_12_out, multiplexer_13_out, multiplexer_14_out, multiplexer_15_out, multiplexer_16_out,
       multiplexer_17_out, multiplexer_18_out, multiplexer_19_out, multiplexer_20_out, multiplexer_21_out,
       multiplexer_22_out, multiplexer_23_out, multiplexer_24_out, multiplexer_25_out, multiplexer_26_out,
       multiplexer_27_out, multiplexer_28_out, multiplexer_29_out, multiplexer_30_out, multiplexer_31_out,
       multiplexer_32_out;

  Multiplexer #(.width(4), .enable("false")) multiplexer_1 (
    .in0(Push_Data), .in1(gpregister_2_data_out), .out(multiplexer_1_out), .sel(Push_Pop));
  Multiplexer #(.width(4), .enable("false")) multiplexer_2 (
    .in0(Pop_Data), .in1(gpregister_3_data_out), .out(multiplexer_2_out), .sel(Push_Pop));
  Multiplexer #(.width(4), .enable("false")) multiplexer_3 (
    .in0(gpregister_2_data_out), .in1(gpregister_4_data_out), .out(multiplexer_3_out), .sel(Push_Pop));
  Multiplexer #(.width(4), .enable("false")) multiplexer_4 (
    .in0(gpregister_3_data_out), .in1(gpregister_5_data_out), .out(multiplexer_4_out), .sel(Push_Pop));
  Multiplexer #(.width(4), .enable("false")) multiplexer_5 (
    .in0(gpregister_4_data_out), .in1(gpregister_6_data_out), .out(multiplexer_5_out), .sel(Push_Pop));
  Multiplexer #(.width(4), .enable("false")) multiplexer_6 (
    .in0(gpregister_5_data_out), .in1(gpregister_7_data_out), .out(multiplexer_6_out), .sel(Push_Pop));
  Multiplexer #(.width(4), .enable("false")) multiplexer_7 (
    .in0(gpregister_6_data_out), .in1(gpregister_8_data_out), .out(multiplexer_7_out), .sel(Push_Pop));
  Multiplexer #(.width(4), .enable("false")) multiplexer_8 (
    .in0(gpregister_7_data_out), .in1(gpregister_9_data_out), .out(multiplexer_8_out), .sel(Push_Pop));
  Multiplexer #(.width(4), .enable("false")) multiplexer_9 (
    .in0(gpregister_8_data_out), .in1(gpregister_10_data_out), .out(multiplexer_9_out), .sel(Push_Pop));
  Multiplexer #(.width(4), .enable("false")) multiplexer_10 (
    .in0(gpregister_9_data_out), .in1(gpregister_11_data_out), .out(multiplexer_10_out), .sel(Push_Pop));
  Multiplexer #(.width(4), .enable("false")) multiplexer_11 (
    .in0(gpregister_10_data_out), .in1(gpregister_12_data_out), .out(multiplexer_11_out), .sel(Push_Pop));
  Multiplexer #(.width(4), .enable("false")) multiplexer_12 (
    .in0(gpregister_11_data_out), .in1(gpregister_13_data_out), .out(multiplexer_12_out), .sel(Push_Pop));
  Multiplexer #(.width(4), .enable("false")) multiplexer_13 (
    .in0(gpregister_12_data_out), .in1(gpregister_14_data_out), .out(multiplexer_13_out), .sel(Push_Pop));
  Multiplexer #(.width(4), .enable("false")) multiplexer_14 (
    .in0(gpregister_13_data_out), .in1(gpregister_15_data_out), .out(multiplexer_14_out), .sel(Push_Pop));
  Multiplexer #(.width(4), .enable("false")) multiplexer_15 (
    .in0(gpregister_14_data_out), .in1(gpregister_16_data_out), .out(multiplexer_15_out), .sel(Push_Pop));
  Multiplexer #(.width(4), .enable("false")) multiplexer_16 (
    .in0(gpregister_15_data_out), .in1(gpregister_17_data_out), .out(multiplexer_16_out), .sel(Push_Pop));
  GPRegister gpregister_1 (.Data_In(multiplexer_1_out), .Data_Out(Pop_Data), .Clock(Clock), .Write(Enabled));
  GPRegister gpregister_2 (
    .Data_In(multiplexer_2_out), .Data_Out(gpregister_2_data_out), .Clock(Clock), .Write(Enabled));
  GPRegister gpregister_3 (
    .Data_In(multiplexer_3_out), .Data_Out(gpregister_3_data_out), .Clock(Clock), .Write(Enabled));
  GPRegister gpregister_4 (
    .Data_In(multiplexer_4_out), .Data_Out(gpregister_4_data_out), .Clock(Clock), .Write(Enabled));
  GPRegister gpregister_5 (
    .Data_In(multiplexer_5_out), .Data_Out(gpregister_5_data_out), .Clock(Clock), .Write(Enabled));
  GPRegister gpregister_6 (
    .Data_In(multiplexer_6_out), .Data_Out(gpregister_6_data_out), .Clock(Clock), .Write(Enabled));
  GPRegister gpregister_7 (
    .Data_In(multiplexer_7_out), .Data_Out(gpregister_7_data_out), .Clock(Clock), .Write(Enabled));
  GPRegister gpregister_8 (
    .Data_In(multiplexer_8_out), .Data_Out(gpregister_8_data_out), .Clock(Clock), .Write(Enabled));
  GPRegister gpregister_9 (
    .Data_In(multiplexer_9_out), .Data_Out(gpregister_9_data_out), .Clock(Clock), .Write(Enabled));
  GPRegister gpregister_10 (
    .Data_In(multiplexer_10_out), .Data_Out(gpregister_10_data_out), .Clock(Clock), .Write(Enabled));
  GPRegister gpregister_11 (
    .Data_In(multiplexer_11_out), .Data_Out(gpregister_11_data_out), .Clock(Clock), .Write(Enabled));
  GPRegister gpregister_12 (
    .Data_In(multiplexer_12_out), .Data_Out(gpregister_12_data_out), .Clock(Clock), .Write(Enabled));
  GPRegister gpregister_13 (
    .Data_In(multiplexer_13_out), .Data_Out(gpregister_13_data_out), .Clock(Clock), .Write(Enabled));
  GPRegister gpregister_14 (
    .Data_In(multiplexer_14_out), .Data_Out(gpregister_14_data_out), .Clock(Clock), .Write(Enabled));
  GPRegister gpregister_15 (
    .Data_In(multiplexer_15_out), .Data_Out(gpregister_15_data_out), .Clock(Clock), .Write(Enabled));
  GPRegister gpregister_16 (
    .Data_In(multiplexer_16_out), .Data_Out(gpregister_16_data_out), .Clock(Clock), .Write(Enabled));
  // Probe on Pop_Data
  // Probe on gpregister_2_data_out
  // Probe on gpregister_3_data_out
  // Probe on gpregister_4_data_out
  // Probe on gpregister_5_data_out
  // Probe on gpregister_6_data_out
  // Probe on gpregister_7_data_out
  // Probe on gpregister_8_data_out
  // Probe on gpregister_9_data_out
  // Probe on gpregister_10_data_out
  // Probe on gpregister_11_data_out
  // Probe on gpregister_12_data_out
  // Probe on gpregister_13_data_out
  // Probe on gpregister_14_data_out
  // Probe on gpregister_15_data_out
  // Probe on gpregister_16_data_out
  Multiplexer #(.width(4), .enable("false")) multiplexer_17 (
    .in0(gpregister_16_data_out), .in1(gpregister_18_data_out), .out(multiplexer_17_out), .sel(Push_Pop));
  Multiplexer #(.width(4), .enable("false")) multiplexer_18 (
    .in0(gpregister_17_data_out), .in1(gpregister_19_data_out), .out(multiplexer_18_out), .sel(Push_Pop));
  Multiplexer #(.width(4), .enable("false")) multiplexer_19 (
    .in0(gpregister_18_data_out), .in1(gpregister_20_data_out), .out(multiplexer_19_out), .sel(Push_Pop));
  Multiplexer #(.width(4), .enable("false")) multiplexer_20 (
    .in0(gpregister_19_data_out), .in1(gpregister_21_data_out), .out(multiplexer_20_out), .sel(Push_Pop));
  Multiplexer #(.width(4), .enable("false")) multiplexer_21 (
    .in0(gpregister_20_data_out), .in1(gpregister_22_data_out), .out(multiplexer_21_out), .sel(Push_Pop));
  Multiplexer #(.width(4), .enable("false")) multiplexer_22 (
    .in0(gpregister_21_data_out), .in1(gpregister_23_data_out), .out(multiplexer_22_out), .sel(Push_Pop));
  Multiplexer #(.width(4), .enable("false")) multiplexer_23 (
    .in0(gpregister_22_data_out), .in1(gpregister_24_data_out), .out(multiplexer_23_out), .sel(Push_Pop));
  Multiplexer #(.width(4), .enable("false")) multiplexer_24 (
    .in0(gpregister_23_data_out), .in1(gpregister_25_data_out), .out(multiplexer_24_out), .sel(Push_Pop));
  Multiplexer #(.width(4), .enable("false")) multiplexer_25 (
    .in0(gpregister_24_data_out), .in1(gpregister_26_data_out), .out(multiplexer_25_out), .sel(Push_Pop));
  Multiplexer #(.width(4), .enable("false")) multiplexer_26 (
    .in0(gpregister_25_data_out), .in1(gpregister_27_data_out), .out(multiplexer_26_out), .sel(Push_Pop));
  Multiplexer #(.width(4), .enable("false")) multiplexer_27 (
    .in0(gpregister_26_data_out), .in1(gpregister_28_data_out), .out(multiplexer_27_out), .sel(Push_Pop));
  Multiplexer #(.width(4), .enable("false")) multiplexer_28 (
    .in0(gpregister_27_data_out), .in1(gpregister_29_data_out), .out(multiplexer_28_out), .sel(Push_Pop));
  Multiplexer #(.width(4), .enable("false")) multiplexer_29 (
    .in0(gpregister_28_data_out), .in1(gpregister_30_data_out), .out(multiplexer_29_out), .sel(Push_Pop));
  Multiplexer #(.width(4), .enable("false")) multiplexer_30 (
    .in0(gpregister_29_data_out), .in1(gpregister_31_data_out), .out(multiplexer_30_out), .sel(Push_Pop));
  Multiplexer #(.width(4), .enable("false")) multiplexer_31 (
    .in0(gpregister_30_data_out), .in1(gpregister_32_data_out), .out(multiplexer_31_out), .sel(Push_Pop));
  Multiplexer #(.width(4), .enable("false")) multiplexer_32 (
    .in0(gpregister_31_data_out), .out(multiplexer_32_out), .sel(Push_Pop));  // open: in1
  GPRegister gpregister_17 (
    .Data_In(multiplexer_17_out), .Data_Out(gpregister_17_data_out), .Clock(Clock), .Write(Enabled));
  GPRegister gpregister_18 (
    .Data_In(multiplexer_18_out), .Data_Out(gpregister_18_data_out), .Clock(Clock), .Write(Enabled));
  GPRegister gpregister_19 (
    .Data_In(multiplexer_19_out), .Data_Out(gpregister_19_data_out), .Clock(Clock), .Write(Enabled));
  GPRegister gpregister_20 (
    .Data_In(multiplexer_20_out), .Data_Out(gpregister_20_data_out), .Clock(Clock), .Write(Enabled));
  GPRegister gpregister_21 (
    .Data_In(multiplexer_21_out), .Data_Out(gpregister_21_data_out), .Clock(Clock), .Write(Enabled));
  GPRegister gpregister_22 (
    .Data_In(multiplexer_22_out), .Data_Out(gpregister_22_data_out), .Clock(Clock), .Write(Enabled));
  GPRegister gpregister_23 (
    .Data_In(multiplexer_23_out), .Data_Out(gpregister_23_data_out), .Clock(Clock), .Write(Enabled));
  GPRegister gpregister_24 (
    .Data_In(multiplexer_24_out), .Data_Out(gpregister_24_data_out), .Clock(Clock), .Write(Enabled));
  GPRegister gpregister_25 (
    .Data_In(multiplexer_25_out), .Data_Out(gpregister_25_data_out), .Clock(Clock), .Write(Enabled));
  GPRegister gpregister_26 (
    .Data_In(multiplexer_26_out), .Data_Out(gpregister_26_data_out), .Clock(Clock), .Write(Enabled));
  GPRegister gpregister_27 (
    .Data_In(multiplexer_27_out), .Data_Out(gpregister_27_data_out), .Clock(Clock), .Write(Enabled));
  GPRegister gpregister_28 (
    .Data_In(multiplexer_28_out), .Data_Out(gpregister_28_data_out), .Clock(Clock), .Write(Enabled));
  GPRegister gpregister_29 (
    .Data_In(multiplexer_29_out), .Data_Out(gpregister_29_data_out), .Clock(Clock), .Write(Enabled));
  GPRegister gpregister_30 (
    .Data_In(multiplexer_30_out), .Data_Out(gpregister_30_data_out), .Clock(Clock), .Write(Enabled));
  GPRegister gpregister_31 (
    .Data_In(multiplexer_31_out), .Data_Out(gpregister_31_data_out), .Clock(Clock), .Write(Enabled));
  GPRegister gpregister_32 (
    .Data_In(multiplexer_32_out), .Data_Out(gpregister_32_data_out), .Clock(Clock), .Write(Enabled));
  // Probe on gpregister_17_data_out
  // Probe on gpregister_18_data_out
  // Probe on gpregister_19_data_out
  // Probe on gpregister_20_data_out
  // Probe on gpregister_21_data_out
  // Probe on gpregister_22_data_out
  // Probe on gpregister_23_data_out
  // Probe on gpregister_24_data_out
  // Probe on gpregister_25_data_out
  // Probe on gpregister_26_data_out
  // Probe on gpregister_27_data_out
  // Probe on gpregister_28_data_out
  // Probe on gpregister_29_data_out
  // Probe on gpregister_30_data_out
  // Probe on gpregister_31_data_out
  // Probe on gpregister_32_data_out
endmodule
