// Logisim project 005z_demo_4bit_MPU.circ as structural Verilog: 9 circuits, main circuit 4 Bit Microprocessor
module _4_Bit_Microprocessor (
  input  in_1,
  input  [2:0] Program_Selection,
  input  Reset
);

  wire ASCII_Enabled, Clock, Jump_Enabled, Jump_Zero_Enabled, Stack_Enabled, Write_Enabled;
  wire [1:0] Register_Data_Select;
  wire [2:0] Addr_A, Addr_B, ALU_Function, Write_Addr;
  wire [3:0] alu_1_alu_output, Data_A, Data_B, multiplexer_1_out, OP_Code, stack_1_pop_data;
  wire [3:3] WriteData;
  wire [7:0] Jump_Address, n8_bit_counter_1_count;
  wire [11:7] program_selector_1_program_output;

  Clock u_Clock (.out(Clock));
  Multiplexer #(.select(2), .width(4), .enable("false")) multiplexer_1 (
    .in0({WriteData[3], Addr_B}), .in1(alu_1_alu_output), .in2(Data_A), .in3(stack_1_pop_data),
    .out(multiplexer_1_out), .sel(Register_Data_Select));
  _8_Bit_Counter u_8_bit_counter_1 (
    .Clock(Clock), .Count(n8_bit_counter_1_count), .Jump_Address(Jump_Address), .Decrement(in_1),
    .Clear(Reset), .Jump_Enabled(Jump_Enabled));
  ROM #(.addrWidth(4)) rom_1 (
    .addr(OP_Code), .data({ALU_Function, Register_Data_Select, ASCII_Enabled, Stack_Enabled, Write_Enabled}));  // open: sel
  // Probe on n8_bit_counter_1_count
  Program_Selector program_selector_1 (
    .Count(n8_bit_counter_1_count),
    .Program_Output({OP_Code, program_selector_1_program_output[11], Write_Addr, program_selector_1_program_output[7], Addr_A, WriteData[3], Addr_B}),
    .Program_Selection(Program_Selection));
  // Probe on {OP_Code, program_selector_1_program_output[11], Write_Addr, program_selector_1_program_output[7], Addr_A, WriteData[3], Addr_B}
  Register_File register_file_1 (
    .Clock(Clock), .Data_In(multiplexer_1_out), .Data_A(Data_A), .Data_B(Data_B),
    .Write_Enabled(Write_Enabled), .Write_Address(Write_Addr), .Read_Address_A(Addr_A),
    .Read_Address_B(Addr_B));
  TTY tty_1 (.data({Data_A[2:0], Data_B}), .clk(Clock), .we(ASCII_Enabled), .clr(Reset));
  ALU alu_1 (
    .Data_A(Data_A), .Data_B(Data_B), .ALU_Output(alu_1_alu_output), .ALU_Function(ALU_Function),
    .Jump_Zero_Enabled(Jump_Zero_Enabled), .Jump_Enabled(Jump_Enabled));
  // Probe on {WriteData[3], Addr_B}
  // Probe on Addr_B
  // Probe on Addr_A
  // Probe on Write_Addr
  // Probe on OP_Code
  // Probe on Write_Enabled
  // Probe on Stack_Enabled
  // Probe on ASCII_Enabled
  // Probe on Register_Data_Select
  // Probe on ALU_Function
  // Probe on Jump_Enabled
  // Probe on Data_A
  // Probe on Data_B
  // Probe on Jump_Address
  Stack stack_1 (
    .Clock(Clock), .Enabled(Stack_Enabled), .Push_Pop(Write_Enabled), .Push_Data({WriteData[3], Addr_B}),
    .Pop_Data(stack_1_pop_data));
  Multiplexer #(.width(8), .enable("false")) multiplexer_2 (
    .in0({Data_B, Data_A}), .in1({1'b0, Write_Addr, WriteData[3], Addr_B}), .out(Jump_Address),
    .sel(Jump_Zero_Enabled));

  // Other names for the same wires on the sheet: WriteData[2:0] = Addr_B

  // Notes on the sheet:
  //   I joined the subtract bit with the ALU function selector bits
  //   View the "Program Selector" module to see the options
  //   Decode the OPCode to instructions
  //   Determine which data to feed to the register file
  //   Use this to select the program to run
  //   contents of rom_1 (hex, n*v repeats v):
  //   0 1 11 4 9 29 49 69 89 a8 c0 2 1b e9
  //   This contains the programs
  //   The register file
  //   Split apart our instructions
  //   ASCII Display
  //   Split apart OPCode Instructions
  //   ALU
  //   Debugging Data
  //   The Stack
  //   The Jump Address Selector
endmodule

module Register_File (
  input  Clock,
  input  [3:0] Data_In,
  input  [2:0] Read_Address_A,
  input  Write_Enabled,
  input  [2:0] Write_Address,
  input  [2:0] Read_Address_B,
  output [3:0] Data_A,
  output [3:0] Data_B
);

  wire W_000, W_001, W_010, W_011, W_100, W_101, W_110, W_111;
  wire [3:0] R_000, R_001, R_010, R_011, R_100, R_101, R_110, R_111;

  Decoder #(.select(3)) decoder_1 (
    .out0(W_000), .out1(W_001), .out2(W_010), .out3(W_011), .out4(W_100), .out5(W_101), .out6(W_110),
    .out7(W_111), .sel(Write_Address), .en(Write_Enabled));
  Register _000 (.Write(W_000), .Clock(Clock), .Data_In(Data_In), .Data_Out(R_000));
  Register _001 (.Write(W_001), .Clock(Clock), .Data_In(Data_In), .Data_Out(R_001));
  Register _010 (.Write(W_010), .Clock(Clock), .Data_In(Data_In), .Data_Out(R_010));
  Register _011 (.Write(W_011), .Clock(Clock), .Data_In(Data_In), .Data_Out(R_011));
  Register _100 (.Write(W_100), .Clock(Clock), .Data_In(Data_In), .Data_Out(R_100));
  Register _101 (.Write(W_101), .Clock(Clock), .Data_In(Data_In), .Data_Out(R_101));
  Register _110 (.Write(W_110), .Clock(Clock), .Data_In(Data_In), .Data_Out(R_110));
  Register _111 (.Write(W_111), .Clock(Clock), .Data_In(Data_In), .Data_Out(R_111));
  Multiplexer #(.select(3), .width(4), .enable("false")) multiplexer_1 (
    .in0(R_000), .in1(R_001), .in2(R_010), .in3(R_011), .in4(R_100), .in5(R_101), .in6(R_110), .in7(R_111),
    .out(Data_A), .sel(Read_Address_A));
  Multiplexer #(.select(3), .width(4), .enable("false")) multiplexer_2 (
    .in0(R_000), .in1(R_001), .in2(R_010), .in3(R_011), .in4(R_100), .in5(R_101), .in6(R_110), .in7(R_111),
    .out(Data_B), .sel(Read_Address_B));
  // Probe on R_000
  // Probe on R_001
  // Probe on R_010
  // Probe on R_011
  // Probe on R_100
  // Probe on R_101
  // Probe on R_110
  // Probe on R_111

  // Notes on the sheet:
  //   Read and Write to the 8 Registers
  //   Our read and write Muxers and Decoders
endmodule

module Register (
  input  Clock,
  input  [3:0] Data_In,
  input  Write,
  output [3:0] Data_Out
);

  wire multiplexer_1_out, multiplexer_2_out, multiplexer_3_out, multiplexer_4_out;

  Multiplexer #(.enable("false")) multiplexer_1 (
    .in0(Data_Out[0]), .in1(Data_In[0]), .out(multiplexer_1_out), .sel(Write));
  Multiplexer #(.enable("false")) multiplexer_2 (
    .in0(Data_Out[1]), .in1(Data_In[1]), .out(multiplexer_2_out), .sel(Write));
  Multiplexer #(.enable("false")) multiplexer_3 (
    .in0(Data_Out[2]), .in1(Data_In[2]), .out(multiplexer_3_out), .sel(Write));
  Multiplexer #(.enable("false")) multiplexer_4 (
    .in0(Data_Out[3]), .in1(Data_In[3]), .out(multiplexer_4_out), .sel(Write));
  D_Flip_Flop d_ff_1 (.clk(Clock), .D(multiplexer_1_out), .Q(Data_Out[0]));  // open: Qn, preset, en, reset
  D_Flip_Flop d_ff_2 (.clk(Clock), .D(multiplexer_2_out), .Q(Data_Out[1]));  // open: Qn, preset, en, reset
  D_Flip_Flop d_ff_3 (.clk(Clock), .D(multiplexer_3_out), .Q(Data_Out[2]));  // open: Qn, preset, en, reset
  D_Flip_Flop d_ff_4 (.clk(Clock), .D(multiplexer_4_out), .Q(Data_Out[3]));  // open: Qn, preset, en, reset

  // Notes on the sheet:
  //   This is a 4 bit Register. It has a write flag and a clock to keep things synchronous
endmodule

module ALU (
  input  [3:0] Data_A,
  input  [3:0] Data_B,
  input  [2:0] ALU_Function,
  output [3:0] ALU_Output,
  output Jump_Enabled,
  output Jump_Zero_Enabled
);

  wire adder_2_carry_out, adder_3_carry_out, adder_4_carry_out, adder_6_carry_out, adder_7_carry_out,
       adder_8_carry_out, Jump_Zero, not_5_out, not_6_out, not_7_out, not_8_out;
  wire [3:0] ADD, AND, MULT, NOT, OR, SUB, XOR;

  Multiplier multiplier_1 (.Data_A(Data_A), .Data_B(Data_B), .Data_Out(MULT));
  xor xor_1 (XOR[3], Data_A[3], Data_B[3]);
  xor xor_2 (XOR[2], Data_A[2], Data_B[2]);
  xor xor_3 (XOR[1], Data_A[1], Data_B[1]);
  xor xor_4 (XOR[0], Data_A[0], Data_B[0]);
  Multiplexer #(.select(3), .width(4), .enable("false")) multiplexer_1 (
    .in0(XOR), .in1(AND), .in2(OR), .in3(ADD), .in4(NOT), .in7(SUB), .out(ALU_Output), .sel(ALU_Function));  // open: in5, in6
  and and_1 (AND[3], Data_A[3], Data_B[3]);
  and and_2 (AND[2], Data_A[2], Data_B[2]);
  and and_3 (AND[1], Data_A[1], Data_B[1]);
  and and_4 (AND[0], Data_A[0], Data_B[0]);
  nor nor_1 (Jump_Zero, Data_A[3], Data_A[2], Data_A[1], Data_A[0]);
  or or_1 (OR[3], Data_A[3], Data_B[3]);
  or or_2 (OR[2], Data_A[2], Data_B[2]);
  or or_3 (OR[1], Data_A[1], Data_B[1]);
  or or_4 (OR[0], Data_A[0], Data_B[0]);
  Multiplexer #(.select(3), .enable("false")) multiplexer_2 (
    .in0(1'b0), .in1(1'b0), .in2(1'b0), .in3(1'b0), .in4(1'b0), .in5(1'b1), .in6(Jump_Zero), .in7(1'b0),
    .out(Jump_Enabled), .sel(ALU_Function));
  Adder adder_1 (.A(Data_A[3]), .B(Data_B[3]), .Sum(ADD[3]), .Carry_In(adder_2_carry_out));  // open: Carry_Out
  Adder adder_2 (
    .A(Data_A[2]), .B(Data_B[2]), .Sum(ADD[2]), .Carry_Out(adder_2_carry_out), .Carry_In(adder_3_carry_out));
  Adder adder_3 (
    .A(Data_A[1]), .B(Data_B[1]), .Sum(ADD[1]), .Carry_Out(adder_3_carry_out), .Carry_In(adder_4_carry_out));
  Adder adder_4 (.A(Data_A[0]), .B(Data_B[0]), .Sum(ADD[0]), .Carry_Out(adder_4_carry_out), .Carry_In(1'b0));
  Multiplexer #(.select(3), .enable("false")) multiplexer_3 (
    .in0(1'b0), .in1(1'b0), .in2(1'b0), .in3(1'b0), .in4(1'b0), .in5(1'b0), .in6(Jump_Zero), .in7(1'b0),
    .out(Jump_Zero_Enabled), .sel(ALU_Function));
  not not_1 (NOT[3], Data_A[3]);
  not not_2 (NOT[2], Data_A[2]);
  not not_3 (NOT[1], Data_A[1]);
  not not_4 (NOT[0], Data_A[0]);
  not not_5 (not_5_out, Data_B[1]);
  not not_6 (not_6_out, Data_B[0]);
  Adder adder_5 (.A(Data_A[3]), .B(not_8_out), .Sum(SUB[3]), .Carry_In(adder_6_carry_out));  // open: Carry_Out
  not not_7 (not_7_out, Data_B[2]);
  not not_8 (not_8_out, Data_B[3]);
  Adder adder_6 (
    .A(Data_A[2]), .B(not_7_out), .Sum(SUB[2]), .Carry_Out(adder_6_carry_out), .Carry_In(adder_7_carry_out));
  Adder adder_7 (
    .A(Data_A[1]), .B(not_5_out), .Sum(SUB[1]), .Carry_Out(adder_7_carry_out), .Carry_In(adder_8_carry_out));
  Adder adder_8 (.A(Data_A[0]), .B(not_6_out), .Sum(SUB[0]), .Carry_Out(adder_8_carry_out), .Carry_In(1'b1));

  // Notes on the sheet:
  //    MULTIPLY (Old) Changed ALU functions to Jumps
  //   000 - XOR
  //   001 - AND
  //   Determine if the data in the register is 0
  //   If Our ALU Function is to Jump, determine if it should be enabled or if the Jump Zero test is successful
  //   010 - OR
  //   011 - ADD
  //   101 - NOT
  //   111 - SUB
endmodule

module Adder (
  input  A,
  input  B,
  input  Carry_In,
  output Sum,
  output Carry_Out
);

  wire and_1_out, and_2_out, xor_1_out;

  xor xor_1 (xor_1_out, A, B);
  xor xor_2 (Sum, xor_1_out, Carry_In);
  and and_1 (and_1_out, xor_1_out, Carry_In);
  and and_2 (and_2_out, A, B);
  or or_1 (Carry_Out, and_1_out, and_2_out);

  // Notes on the sheet:
  //   Single Bit Adder With Carry Output
endmodule

module Multiplier (
  input  [3:0] Data_A,
  input  [3:0] Data_B,
  output [3:0] Data_Out
);

  wire adder_1_carry_out, adder_1_sum, adder_2_carry_out, adder_2_sum, adder_3_carry_out, adder_3_sum,
       adder_4_carry_out, adder_5_carry_out, adder_5_sum, adder_6_carry_out, adder_6_sum, adder_7_carry_out,
       adder_7_sum, adder_8_carry_out, adder_10_carry_out, adder_11_carry_out, adder_12_carry_out, and_1_out,
       and_2_out, and_3_out, and_4_out, and_5_out, and_6_out, and_7_out, and_9_out, and_10_out, and_11_out,
       and_12_out, and_13_out, and_14_out, and_15_out, and_16_out;

  and and_1 (and_1_out, Data_A[3], Data_B[1]);
  and and_2 (and_2_out, Data_A[2], Data_B[1]);
  and and_3 (and_3_out, Data_A[1], Data_B[1]);
  and and_4 (and_4_out, Data_A[0], Data_B[1]);
  and and_5 (and_5_out, Data_A[3], Data_B[0]);
  and and_6 (and_6_out, Data_A[2], Data_B[0]);
  and and_7 (and_7_out, Data_A[1], Data_B[0]);
  and and_8 (Data_Out[0], Data_A[0], Data_B[0]);
  and and_9 (and_9_out, Data_A[3], Data_B[2]);
  and and_10 (and_10_out, Data_A[2], Data_B[2]);
  and and_11 (and_11_out, Data_A[1], Data_B[2]);
  and and_12 (and_12_out, Data_A[0], Data_B[2]);
  and and_13 (and_13_out, Data_A[3], Data_B[3]);
  and and_14 (and_14_out, Data_A[2], Data_B[3]);
  and and_15 (and_15_out, Data_A[1], Data_B[3]);
  and and_16 (and_16_out, Data_A[0], Data_B[3]);
  Adder adder_1 (
    .A(1'b0), .B(and_1_out), .Sum(adder_1_sum), .Carry_Out(adder_1_carry_out), .Carry_In(adder_2_carry_out));
  Adder adder_2 (
    .A(and_5_out), .B(and_2_out), .Sum(adder_2_sum), .Carry_Out(adder_2_carry_out),
    .Carry_In(adder_3_carry_out));
  Adder adder_3 (
    .A(and_6_out), .B(and_3_out), .Sum(adder_3_sum), .Carry_Out(adder_3_carry_out),
    .Carry_In(adder_4_carry_out));
  Adder adder_4 (.A(and_7_out), .B(and_4_out), .Sum(Data_Out[1]), .Carry_Out(adder_4_carry_out), .Carry_In(1'b0));
  Adder adder_5 (
    .A(adder_1_carry_out), .B(and_9_out), .Sum(adder_5_sum), .Carry_Out(adder_5_carry_out),
    .Carry_In(adder_6_carry_out));
  Adder adder_6 (
    .A(adder_1_sum), .B(and_10_out), .Sum(adder_6_sum), .Carry_Out(adder_6_carry_out),
    .Carry_In(adder_7_carry_out));
  Adder adder_7 (
    .A(adder_2_sum), .B(and_11_out), .Sum(adder_7_sum), .Carry_Out(adder_7_carry_out),
    .Carry_In(adder_8_carry_out));
  Adder adder_8 (.A(adder_3_sum), .B(and_12_out), .Sum(Data_Out[2]), .Carry_Out(adder_8_carry_out), .Carry_In(1'b0));
  Adder adder_9 (.A(adder_5_carry_out), .B(and_13_out), .Carry_In(adder_10_carry_out));  // open: Sum, Carry_Out
  Adder adder_10 (
    .A(adder_5_sum), .B(and_14_out), .Carry_Out(adder_10_carry_out), .Carry_In(adder_11_carry_out));  // open: Sum
  Adder adder_11 (
    .A(adder_6_sum), .B(and_15_out), .Carry_Out(adder_11_carry_out), .Carry_In(adder_12_carry_out));  // open: Sum
  Adder adder_12 (.A(adder_7_sum), .B(and_16_out), .Sum(Data_Out[3]), .Carry_Out(adder_12_carry_out), .Carry_In(1'b0));

  // Other names for the same wires on the sheet: A0 = Data_A[0]; A1 = Data_A[1]; A2 = Data_A[2]; A3 = Data_A[3];
  //   B0 = Data_B[0]; B1 = Data_B[1]; B2 = Data_B[2]; B3 = Data_B[3]

  // Notes on the sheet:
  //   Each bit needs to be AND'ed with the other bits then added together
  //   Take the input and split the bits up
  //   Our output bit, overflow is ignored as we are only a 4 bit system
endmodule

module Program_Selector (
  input  [7:0] Count,
  input  [2:0] Program_Selection,
  output [15:0] Program_Output
);

  wire [15:0] rom_1_data, rom_2_data, rom_3_data, rom_4_data, rom_5_data, rom_6_data, rom_7_data, rom_8_data;

  ROM #(.dataWidth(16)) rom_1 (.addr(Count), .data(rom_1_data));  // open: sel
  ROM #(.dataWidth(16)) rom_2 (.addr(Count), .data(rom_2_data));  // open: sel
  ROM #(.dataWidth(16)) rom_3 (.addr(Count), .data(rom_3_data));  // open: sel
  ROM #(.dataWidth(16)) rom_4 (.addr(Count), .data(rom_4_data));  // open: sel
  ROM #(.dataWidth(16)) rom_5 (.addr(Count), .data(rom_5_data));  // open: sel
  ROM #(.dataWidth(16)) rom_6 (.addr(Count), .data(rom_6_data));  // open: sel
  ROM #(.dataWidth(16)) rom_7 (.addr(Count), .data(rom_7_data));  // open: sel
  ROM #(.dataWidth(16)) rom_8 (.addr(Count), .data(rom_8_data));  // open: sel
  Multiplexer #(.select(3), .width(16), .enable("false")) multiplexer_1 (
    .in0(rom_1_data), .in1(rom_2_data), .in2(rom_3_data), .in3(rom_4_data), .in4(rom_5_data),
    .in5(rom_6_data), .in6(rom_7_data), .in7(rom_8_data), .out(Program_Output), .sel(Program_Selection));

  // Notes on the sheet:
  //   000 - Arithmatic (Sample Program)
  //   001 - Hello World
  //   010 - Simple Things
  //   011 - ALU Tester
  //   100 - Display Function
  //   contents of rom_1 (hex, n*v repeats v):
  //   0 1204 1302 1401 7523 7654 1103 3016
  //   contents of rom_2 (hex, n*v repeats v):
  //   1004 1108 3001 1206 1305 3023 1406 150c 3045 3045 1606 170f 3067 1002 1100 3001 1205 1307 3023 1406
  //   150f 3045 1607 1702 3067 1006 110c 3001 1206 1304 3023 1402 1501 3045
  //   contents of rom_3 (hex, n*v repeats v):
  //   1004 1102 3001 1207 1309 3023 1402 1500 3045 1607 1703 3067 1006 110d 3001 1206 1301 3023 1406 150c
  //   3045 1606 170c 3067 1002 1100 3001 1206 1301 3023 1406 150e 3045 1606 1704 3067 1002 1100 3001 1207
  //   1303 3023 1406 1509 3045 1606 170d 3067 1007 1100 3001 1206 130c 3023 1406 1505 3045 1002 1100 3001
  //   1207 1304 3023 1406 1508 3045 1606 1709 3067 1006 110e 3001 1206 1307 3023 1407 1503 3045 1602 1700
  //   3067 1006 1101 3001 1207 1302 3023 1406 1505 3045 1600 170a 3067 1006 1107 3001 1207 1302 3023 1406
  //   1505 3045 1606 1701 3067 1007 1104 3001 1202 1300 3023 1407 1504 3045 1606 1708 3067 1006 1109 3001
  //   1206 130e 3023 1406 1507 3045 1607 1703 3067 1002 1100 3001 1206 1302 3023 1407 1502 3045 1606 170f
  //   3067 1007 1105 3001 1206 1307 3023 1406 1508 3045 1607 1704 3067 1002 1100 3001 1207 1304 3023 1406
  //   150f 3045 1602 1700 3067 1007 1100 3001 1206 1301 3023 1407 1503 3045 1607 1703 3067 1002 1101 3001
  //   3001 1200 130a 3023 3023
  //   contents of rom_4 (hex, n*v repeats v):
  //   1703 1004 1105 3070 1202 1300 3023 1205 1308 3023 1204 130f 3023 1205 1302 3023 1202 1300 3023 3071
  //   1202 1300 3023 1203 130d 3023 1202 1300 3023 4301 3073 1200 130a 3023 1007 1105 3070 1202 1300 3023
  //   1204 1301 3023 1204 130e 3023 1204 1304 3023 1202 1300 3023 3071 1202 1300 3023 1203 130d 3023 1202
  //   1300 3023 5301 3073 1200 130a 3023 1003 1105 3070 1202 1300 3023 1204 130f 3023 1205 1302 3023 1202
  //   1300 3023 3071 1202 1300 3023 1203 130d 3023 1202 1300 3023 6401 3074 1200 130a 3023 1002 1105 3070
  //   1202 1300 3023 1202 130b 3023 1202 1300 3023 3071 1202 1300 3023 1203 130d 3023 1202 1300 3023 7301
  //   3073 1200 130a 3023 1007 1103 3070 1202 1300 3023 1202 130d 3023 1202 1300 3023 3071 1202 1300 3023
  //   1203 130d 3023 1202 1300 3023 f301 3073 1200 130a 3023
  //   contents of rom_5 (hex, n*v repeats v):
  //   1000 a00c c100 c000 6201 a029 3001 1700 a072 c000 c100 9001 b001 b006 b000 b000 b004 b009 b004 b008
  //   1000 a002 1002 1101 3001
  //   contents of rom_6 (hex, n*v repeats v):
  //   0 1204 1302 1401 7523 7654 1103 3016
  //   contents of rom_7 (hex, n*v repeats v):
  //   b000 204b 1302 1401 7523 7654 1103 3016
  //   contents of rom_8 (hex, n*v repeats v):
  //   1000 a109 c100 c000 6201 a029 3001 1700 a072 c000 c100 9001 1600 c100 c000 6206 a124 7101 1700 a07e
  //   1703 3071 c000 c100 9001 b003 b003 b000 b000 b000 b00d b005 b003 b004 b002 b002 b000 b002 b00c b006
  //   b00f b006 b00c b006 b00c b006 b005 b004 b008 1000 a002 b004 b009 b000 b000 b002 b000 b003 b00d b002
  //   b000 b003 b004 b002 b000 b002 b00b b002 b000 b003 b003 1000 a002 b005 b000 b000 b003 b004 1000 a00c
  //   1000 110d 3001 b006 b009 b000 b000 b002 b000 b003 b00d b002 b000 b003 b003 b002 b000 b002 b00a b002
  //   b000 b003 b003 1000 a002 b007 b001 b000 b003 b003 b003 1000 a00c 1000 110d 3001 b008 b00a b000 b000
  //   b002 b000 b003 b00d b002 b000 b003 b003 b002 b000 b002 b00d b002 b000 b003 b004 1000 a002 1004 1103
  //   8110 1201 7112 7210 1703 3072 1000 110d 3001 b00a b00b b000 b000 b002 b000 b003 b00d b002 b000 b003
  //   b002 b002 b000 b002 b00d b002 b000 b003 b005 1000 a002 1005 1102 d201 1703 3072 1000 110d 3001
endmodule

module Stack (
  input  Clock,
  input  Enabled,
  input  Push_Pop,
  input  [3:0] Push_Data,
  output [3:0] Pop_Data
);

  wire [3:0] multiplexer_1_out, multiplexer_2_out, multiplexer_3_out, multiplexer_4_out, multiplexer_5_out,
       multiplexer_6_out, multiplexer_7_out, multiplexer_8_out, multiplexer_9_out, multiplexer_10_out,
       multiplexer_11_out, multiplexer_12_out, multiplexer_13_out, multiplexer_14_out, multiplexer_15_out,
       multiplexer_16_out, multiplexer_17_out, multiplexer_18_out, multiplexer_19_out, multiplexer_20_out,
       multiplexer_21_out, multiplexer_22_out, multiplexer_23_out, multiplexer_24_out, multiplexer_25_out,
       multiplexer_26_out, multiplexer_27_out, multiplexer_28_out, multiplexer_29_out, multiplexer_30_out,
       multiplexer_31_out, multiplexer_32_out, register_2_data_out, register_3_data_out, register_4_data_out,
       register_5_data_out, register_6_data_out, register_7_data_out, register_8_data_out,
       register_9_data_out, register_10_data_out, register_11_data_out, register_12_data_out,
       register_13_data_out, register_14_data_out, register_15_data_out, register_16_data_out,
       register_17_data_out, register_18_data_out, register_19_data_out, register_20_data_out,
       register_21_data_out, register_22_data_out, register_23_data_out, register_24_data_out,
       register_25_data_out, register_26_data_out, register_27_data_out, register_28_data_out,
       register_29_data_out, register_30_data_out, register_31_data_out, register_32_data_out;

  Multiplexer #(.width(4), .enable("false")) multiplexer_1 (
    .in0(Push_Data), .in1(register_2_data_out), .out(multiplexer_1_out), .sel(Push_Pop));
  Multiplexer #(.width(4), .enable("false")) multiplexer_2 (
    .in0(Pop_Data), .in1(register_3_data_out), .out(multiplexer_2_out), .sel(Push_Pop));
  Multiplexer #(.width(4), .enable("false")) multiplexer_3 (
    .in0(register_2_data_out), .in1(register_4_data_out), .out(multiplexer_3_out), .sel(Push_Pop));
  Multiplexer #(.width(4), .enable("false")) multiplexer_4 (
    .in0(register_3_data_out), .in1(register_5_data_out), .out(multiplexer_4_out), .sel(Push_Pop));
  Multiplexer #(.width(4), .enable("false")) multiplexer_5 (
    .in0(register_4_data_out), .in1(register_6_data_out), .out(multiplexer_5_out), .sel(Push_Pop));
  Multiplexer #(.width(4), .enable("false")) multiplexer_6 (
    .in0(register_5_data_out), .in1(register_7_data_out), .out(multiplexer_6_out), .sel(Push_Pop));
  Multiplexer #(.width(4), .enable("false")) multiplexer_7 (
    .in0(register_6_data_out), .in1(register_8_data_out), .out(multiplexer_7_out), .sel(Push_Pop));
  Multiplexer #(.width(4), .enable("false")) multiplexer_8 (
    .in0(register_7_data_out), .in1(register_9_data_out), .out(multiplexer_8_out), .sel(Push_Pop));
  Multiplexer #(.width(4), .enable("false")) multiplexer_9 (
    .in0(register_8_data_out), .in1(register_10_data_out), .out(multiplexer_9_out), .sel(Push_Pop));
  Multiplexer #(.width(4), .enable("false")) multiplexer_10 (
    .in0(register_9_data_out), .in1(register_11_data_out), .out(multiplexer_10_out), .sel(Push_Pop));
  Multiplexer #(.width(4), .enable("false")) multiplexer_11 (
    .in0(register_10_data_out), .in1(register_12_data_out), .out(multiplexer_11_out), .sel(Push_Pop));
  Multiplexer #(.width(4), .enable("false")) multiplexer_12 (
    .in0(register_11_data_out), .in1(register_13_data_out), .out(multiplexer_12_out), .sel(Push_Pop));
  Multiplexer #(.width(4), .enable("false")) multiplexer_13 (
    .in0(register_12_data_out), .in1(register_14_data_out), .out(multiplexer_13_out), .sel(Push_Pop));
  Multiplexer #(.width(4), .enable("false")) multiplexer_14 (
    .in0(register_13_data_out), .in1(register_15_data_out), .out(multiplexer_14_out), .sel(Push_Pop));
  Multiplexer #(.width(4), .enable("false")) multiplexer_15 (
    .in0(register_14_data_out), .in1(register_16_data_out), .out(multiplexer_15_out), .sel(Push_Pop));
  Multiplexer #(.width(4), .enable("false")) multiplexer_16 (
    .in0(register_15_data_out), .in1(register_17_data_out), .out(multiplexer_16_out), .sel(Push_Pop));
  Register register_1 (.Write(Enabled), .Clock(Clock), .Data_In(multiplexer_1_out), .Data_Out(Pop_Data));
  Register register_2 (.Write(Enabled), .Clock(Clock), .Data_In(multiplexer_2_out), .Data_Out(register_2_data_out));
  Register register_3 (.Write(Enabled), .Clock(Clock), .Data_In(multiplexer_3_out), .Data_Out(register_3_data_out));
  Register register_4 (.Write(Enabled), .Clock(Clock), .Data_In(multiplexer_4_out), .Data_Out(register_4_data_out));
  Register register_5 (.Write(Enabled), .Clock(Clock), .Data_In(multiplexer_5_out), .Data_Out(register_5_data_out));
  Register register_6 (.Write(Enabled), .Clock(Clock), .Data_In(multiplexer_6_out), .Data_Out(register_6_data_out));
  Register register_7 (.Write(Enabled), .Clock(Clock), .Data_In(multiplexer_7_out), .Data_Out(register_7_data_out));
  Register register_8 (.Write(Enabled), .Clock(Clock), .Data_In(multiplexer_8_out), .Data_Out(register_8_data_out));
  Register register_9 (.Write(Enabled), .Clock(Clock), .Data_In(multiplexer_9_out), .Data_Out(register_9_data_out));
  Register register_10 (.Write(Enabled), .Clock(Clock), .Data_In(multiplexer_10_out), .Data_Out(register_10_data_out));
  Register register_11 (.Write(Enabled), .Clock(Clock), .Data_In(multiplexer_11_out), .Data_Out(register_11_data_out));
  Register register_12 (.Write(Enabled), .Clock(Clock), .Data_In(multiplexer_12_out), .Data_Out(register_12_data_out));
  Register register_13 (.Write(Enabled), .Clock(Clock), .Data_In(multiplexer_13_out), .Data_Out(register_13_data_out));
  Register register_14 (.Write(Enabled), .Clock(Clock), .Data_In(multiplexer_14_out), .Data_Out(register_14_data_out));
  Register register_15 (.Write(Enabled), .Clock(Clock), .Data_In(multiplexer_15_out), .Data_Out(register_15_data_out));
  Register register_16 (.Write(Enabled), .Clock(Clock), .Data_In(multiplexer_16_out), .Data_Out(register_16_data_out));
  // Probe on Pop_Data
  // Probe on register_2_data_out
  // Probe on register_3_data_out
  // Probe on register_4_data_out
  // Probe on register_5_data_out
  // Probe on register_6_data_out
  // Probe on register_7_data_out
  // Probe on register_8_data_out
  // Probe on register_9_data_out
  // Probe on register_10_data_out
  // Probe on register_11_data_out
  // Probe on register_12_data_out
  // Probe on register_13_data_out
  // Probe on register_14_data_out
  // Probe on register_15_data_out
  // Probe on register_16_data_out
  Multiplexer #(.width(4), .enable("false")) multiplexer_17 (
    .in0(register_16_data_out), .in1(register_18_data_out), .out(multiplexer_17_out), .sel(Push_Pop));
  Multiplexer #(.width(4), .enable("false")) multiplexer_18 (
    .in0(register_17_data_out), .in1(register_19_data_out), .out(multiplexer_18_out), .sel(Push_Pop));
  Multiplexer #(.width(4), .enable("false")) multiplexer_19 (
    .in0(register_18_data_out), .in1(register_20_data_out), .out(multiplexer_19_out), .sel(Push_Pop));
  Multiplexer #(.width(4), .enable("false")) multiplexer_20 (
    .in0(register_19_data_out), .in1(register_21_data_out), .out(multiplexer_20_out), .sel(Push_Pop));
  Multiplexer #(.width(4), .enable("false")) multiplexer_21 (
    .in0(register_20_data_out), .in1(register_22_data_out), .out(multiplexer_21_out), .sel(Push_Pop));
  Multiplexer #(.width(4), .enable("false")) multiplexer_22 (
    .in0(register_21_data_out), .in1(register_23_data_out), .out(multiplexer_22_out), .sel(Push_Pop));
  Multiplexer #(.width(4), .enable("false")) multiplexer_23 (
    .in0(register_22_data_out), .in1(register_24_data_out), .out(multiplexer_23_out), .sel(Push_Pop));
  Multiplexer #(.width(4), .enable("false")) multiplexer_24 (
    .in0(register_23_data_out), .in1(register_25_data_out), .out(multiplexer_24_out), .sel(Push_Pop));
  Multiplexer #(.width(4), .enable("false")) multiplexer_25 (
    .in0(register_24_data_out), .in1(register_26_data_out), .out(multiplexer_25_out), .sel(Push_Pop));
  Multiplexer #(.width(4), .enable("false")) multiplexer_26 (
    .in0(register_25_data_out), .in1(register_27_data_out), .out(multiplexer_26_out), .sel(Push_Pop));
  Multiplexer #(.width(4), .enable("false")) multiplexer_27 (
    .in0(register_26_data_out), .in1(register_28_data_out), .out(multiplexer_27_out), .sel(Push_Pop));
  Multiplexer #(.width(4), .enable("false")) multiplexer_28 (
    .in0(register_27_data_out), .in1(register_29_data_out), .out(multiplexer_28_out), .sel(Push_Pop));
  Multiplexer #(.width(4), .enable("false")) multiplexer_29 (
    .in0(register_28_data_out), .in1(register_30_data_out), .out(multiplexer_29_out), .sel(Push_Pop));
  Multiplexer #(.width(4), .enable("false")) multiplexer_30 (
    .in0(register_29_data_out), .in1(register_31_data_out), .out(multiplexer_30_out), .sel(Push_Pop));
  Multiplexer #(.width(4), .enable("false")) multiplexer_31 (
    .in0(register_30_data_out), .in1(register_32_data_out), .out(multiplexer_31_out), .sel(Push_Pop));
  Multiplexer #(.width(4), .enable("false")) multiplexer_32 (
    .in0(register_31_data_out), .out(multiplexer_32_out), .sel(Push_Pop));  // open: in1
  Register register_17 (.Write(Enabled), .Clock(Clock), .Data_In(multiplexer_17_out), .Data_Out(register_17_data_out));
  Register register_18 (.Write(Enabled), .Clock(Clock), .Data_In(multiplexer_18_out), .Data_Out(register_18_data_out));
  Register register_19 (.Write(Enabled), .Clock(Clock), .Data_In(multiplexer_19_out), .Data_Out(register_19_data_out));
  Register register_20 (.Write(Enabled), .Clock(Clock), .Data_In(multiplexer_20_out), .Data_Out(register_20_data_out));
  Register register_21 (.Write(Enabled), .Clock(Clock), .Data_In(multiplexer_21_out), .Data_Out(register_21_data_out));
  Register register_22 (.Write(Enabled), .Clock(Clock), .Data_In(multiplexer_22_out), .Data_Out(register_22_data_out));
  Register register_23 (.Write(Enabled), .Clock(Clock), .Data_In(multiplexer_23_out), .Data_Out(register_23_data_out));
  Register register_24 (.Write(Enabled), .Clock(Clock), .Data_In(multiplexer_24_out), .Data_Out(register_24_data_out));
  Register register_25 (.Write(Enabled), .Clock(Clock), .Data_In(multiplexer_25_out), .Data_Out(register_25_data_out));
  Register register_26 (.Write(Enabled), .Clock(Clock), .Data_In(multiplexer_26_out), .Data_Out(register_26_data_out));
  Register register_27 (.Write(Enabled), .Clock(Clock), .Data_In(multiplexer_27_out), .Data_Out(register_27_data_out));
  Register register_28 (.Write(Enabled), .Clock(Clock), .Data_In(multiplexer_28_out), .Data_Out(register_28_data_out));
  Register register_29 (.Write(Enabled), .Clock(Clock), .Data_In(multiplexer_29_out), .Data_Out(register_29_data_out));
  Register register_30 (.Write(Enabled), .Clock(Clock), .Data_In(multiplexer_30_out), .Data_Out(register_30_data_out));
  Register register_31 (.Write(Enabled), .Clock(Clock), .Data_In(multiplexer_31_out), .Data_Out(register_31_data_out));
  Register register_32 (.Write(Enabled), .Clock(Clock), .Data_In(multiplexer_32_out), .Data_Out(register_32_data_out));
  // Probe on register_17_data_out
  // Probe on register_18_data_out
  // Probe on register_19_data_out
  // Probe on register_20_data_out
  // Probe on register_21_data_out
  // Probe on register_22_data_out
  // Probe on register_23_data_out
  // Probe on register_24_data_out
  // Probe on register_25_data_out
  // Probe on register_26_data_out
  // Probe on register_27_data_out
  // Probe on register_28_data_out
  // Probe on register_29_data_out
  // Probe on register_30_data_out
  // Probe on register_31_data_out
  // Probe on register_32_data_out

  // Notes on the sheet:
  //   It goes down for 16 nibbles
  //   And then 16 more
endmodule

module _8_Bit_Counter (
  input  Clock,
  input  [7:0] Jump_Address,
  input  Decrement,
  input  Clear,
  input  Jump_Enabled,
  output [7:0] Count
);

  wire adder_2_carry_out, adder_3_carry_out, adder_4_carry_out, adder_5_carry_out, adder_6_carry_out,
       adder_7_carry_out, adder_8_carry_out, adder_10_carry_out, adder_11_carry_out, adder_12_carry_out,
       adder_13_carry_out, adder_14_carry_out, adder_15_carry_out, adder_16_carry_out;
  wire [1:0] or_2_out;
  wire [7:0] Count__1, Count__1_t, multiplexer_1_out;

  or or_1 (or_2_out[1], Clear, Jump_Enabled);
  or or_2 (or_2_out[0], Decrement, Clear);
  Multiplexer #(.select(2), .width(8), .enable("false")) multiplexer_1 (
    .in0(Count__1), .in1(Count__1_t), .in2(Jump_Address), .in3({8{1'b0}}), .out(multiplexer_1_out),
    .sel(or_2_out));
  D_Flip_Flop d_ff_1 (.clk(Clock), .D(multiplexer_1_out[7]), .Q(Count[7]));  // open: Qn, preset, en, reset
  D_Flip_Flop d_ff_2 (.clk(Clock), .D(multiplexer_1_out[6]), .Q(Count[6]));  // open: Qn, preset, en, reset
  D_Flip_Flop d_ff_3 (.clk(Clock), .D(multiplexer_1_out[5]), .Q(Count[5]));  // open: Qn, preset, en, reset
  D_Flip_Flop d_ff_4 (.clk(Clock), .D(multiplexer_1_out[4]), .Q(Count[4]));  // open: Qn, preset, en, reset
  D_Flip_Flop d_ff_5 (.clk(Clock), .D(multiplexer_1_out[3]), .Q(Count[3]));  // open: Qn, preset, en, reset
  D_Flip_Flop d_ff_6 (.clk(Clock), .D(multiplexer_1_out[2]), .Q(Count[2]));  // open: Qn, preset, en, reset
  D_Flip_Flop d_ff_7 (.clk(Clock), .D(multiplexer_1_out[1]), .Q(Count[1]));  // open: Qn, preset, en, reset
  D_Flip_Flop d_ff_8 (.clk(Clock), .D(multiplexer_1_out[0]), .Q(Count[0]));  // open: Qn, preset, en, reset
  Adder adder_1 (.A(Count[7]), .B(1'b0), .Sum(Count__1[7]), .Carry_In(adder_2_carry_out));  // open: Carry_Out
  Adder adder_2 (
    .A(Count[6]), .B(1'b0), .Sum(Count__1[6]), .Carry_Out(adder_2_carry_out), .Carry_In(adder_3_carry_out));
  Adder adder_3 (
    .A(Count[5]), .B(1'b0), .Sum(Count__1[5]), .Carry_Out(adder_3_carry_out), .Carry_In(adder_4_carry_out));
  Adder adder_4 (
    .A(Count[4]), .B(1'b0), .Sum(Count__1[4]), .Carry_Out(adder_4_carry_out), .Carry_In(adder_5_carry_out));
  Adder adder_5 (
    .A(Count[3]), .B(1'b0), .Sum(Count__1[3]), .Carry_Out(adder_5_carry_out), .Carry_In(adder_6_carry_out));
  Adder adder_6 (
    .A(Count[2]), .B(1'b0), .Sum(Count__1[2]), .Carry_Out(adder_6_carry_out), .Carry_In(adder_7_carry_out));
  Adder adder_7 (
    .A(Count[1]), .B(1'b0), .Sum(Count__1[1]), .Carry_Out(adder_7_carry_out), .Carry_In(adder_8_carry_out));
  Adder adder_8 (.A(Count[0]), .B(1'b1), .Sum(Count__1[0]), .Carry_Out(adder_8_carry_out), .Carry_In(1'b0));
  Adder adder_9 (.A(Count[7]), .B(1'b1), .Sum(Count__1_t[7]), .Carry_In(adder_10_carry_out));  // open: Carry_Out
  Adder adder_10 (
    .A(Count[6]), .B(1'b1), .Sum(Count__1_t[6]), .Carry_Out(adder_10_carry_out), .Carry_In(adder_11_carry_out));
  Adder adder_11 (
    .A(Count[5]), .B(1'b1), .Sum(Count__1_t[5]), .Carry_Out(adder_11_carry_out), .Carry_In(adder_12_carry_out));
  Adder adder_12 (
    .A(Count[4]), .B(1'b1), .Sum(Count__1_t[4]), .Carry_Out(adder_12_carry_out), .Carry_In(adder_13_carry_out));
  Adder adder_13 (
    .A(Count[3]), .B(1'b1), .Sum(Count__1_t[3]), .Carry_Out(adder_13_carry_out), .Carry_In(adder_14_carry_out));
  Adder adder_14 (
    .A(Count[2]), .B(1'b1), .Sum(Count__1_t[2]), .Carry_Out(adder_14_carry_out), .Carry_In(adder_15_carry_out));
  Adder adder_15 (
    .A(Count[1]), .B(1'b1), .Sum(Count__1_t[1]), .Carry_Out(adder_15_carry_out), .Carry_In(adder_16_carry_out));
  Adder adder_16 (.A(Count[0]), .B(1'b0), .Sum(Count__1_t[0]), .Carry_Out(adder_16_carry_out), .Carry_In(1'b1));

  // Other names for the same wires on the sheet: Jump_Addr[7:0] = Jump_Address

  // Notes on the sheet:
  //   I made my own clock to handle jumps
  //   The built in one only worked if the current count was 00
  //   And I couldn't even get that to work
  //   I could have made reset asynchronous, but that's tedious
  //   Adder +1
  //   Subtractor -1
endmodule
