// Logisim project 006_RAM_demo.circ as structural Verilog: 1 circuit, main circuit main
module main (
  input  [7:0] Jump_Address,
  input  Jump_Enabled,
  input  [7:0] in_3,
  input  MemSelect,
  input  [7:0] in_5,
  input  R_W,
  input  RST,
  output [7:0] out_8,
  output [7:0] out_9
);

  wire clock_1_out, decoder_1_out0, decoder_1_out1, not_1_out, not_2_out;
  wire [7:0] Counter_q, multiplexer_1_out, ram_1_data, ram_2_data;

  Multiplexer #(.width(8), .enable("false")) multiplexer_1 (
    .in1(Jump_Address), .out(multiplexer_1_out), .sel(Jump_Enabled));  // open: in0
  Counter Counter (
    .load(Jump_Enabled), .D(multiplexer_1_out), .count(1'b0), .Q(Counter_q), .clk(clock_1_out));  // open: carry, clr
  Decoder #(.enable("false")) decoder_1 (.out0(decoder_1_out0), .out1(decoder_1_out1), .sel(MemSelect));
  Clock clock_1 (.out(clock_1_out));
  RAM ram_1 (.addr(Counter_q), .data(ram_1_data), .sel(decoder_1_out0), .clk(clock_1_out), .ld(R_W), .clr(RST));
  assign ram_1_data = not_1_out ? in_3 : 8'bz;  // Controlled_Buffer controlled_buffer_1
  RAM ram_2 (.addr(Counter_q), .data(ram_2_data), .sel(decoder_1_out1), .clk(clock_1_out), .ld(R_W), .clr(RST));
  assign ram_2_data = not_2_out ? in_5 : 8'bz;  // Controlled_Buffer controlled_buffer_2
  assign out_8 = R_W ? ram_1_data : 8'bz;  // Controlled_Buffer controlled_buffer_3
  not not_1 (not_1_out, R_W);
  assign out_9 = R_W ? ram_2_data : 8'bz;  // Controlled_Buffer controlled_buffer_4
  not not_2 (not_2_out, R_W);

  // Notes on the sheet:
  //   Mem0
  //   Mem1
endmodule
